# Fritzing sketch PowerMon (saved by Fritzing 0.7.10b)
breadboards: 1

parts:
  R1 = Resistor [tolerance=±5% resistance=100 package=THT]
  R2 = Resistor [tolerance=±5% resistance=10k package=THT]
  R3 = Resistor [tolerance=±5% resistance=10k package=THT]
  C1 = Ceramic Capacitor [capacitance=10µF voltage=35V package="100 mil [THT, multilayer]"]
  CT = Inductor [package="400 mil [THT]"]
  Arduino1 = Arduino
  R4 = Resistor [tolerance=±5% resistance=10k package=THT]
  R5 = Resistor [tolerance=±5% resistance=10k package=THT]
  C2 = Ceramic Capacitor [capacitance=10µF voltage=35V package="100 mil [THT, multilayer]"]
  R6 = Resistor [tolerance=±5% resistance=80k package=THT]
  R7 = Resistor [tolerance=±5% resistance=10k package=THT]
  Power_9VAC = Power plug

nets:
  N1: R1.Pin_0, R2.Pin_1, R3.Pin_0, C1.1, CT.pin_0
  N2: R1.Pin_1, CT.pin_1, Arduino1.A0
  N3: R2.Pin_0, Arduino1.+5V, R4.Pin_0
  N4: R3.Pin_1, C1.0, Arduino1.GND, R5.Pin_1, C2.0
  N5: Arduino1.A1, R6.Pin_1, R7.Pin_0
  N6: R4.Pin_1, R5.Pin_0, C2.1, R6.Pin_0, Power_9VAC.GND
  N7: R7.Pin_1, Power_9VAC.VCC
